// Logisim project Atividade de ADD, NOT, OR e AND.circ as structural Verilog: 1 circuit, main circuit main
module main (
  input  [7:0] Entrada,
  input  [7:0] Entrada_2,
  input  [1:0] _00___soma__01___NOT__10___OR__11___AND,
  output [7:0] \Saída 
);

  wire [7:0] adder_1_out, and_1_out, not_1_out, or_1_out;

  Adder adder_1 (.a(Entrada), .b(Entrada_2), .out(adder_1_out));  // open: cin, cout
  assign not_1_out = ~Entrada;  // NOT_Gate not_1, 8 bits wide
  assign and_1_out = Entrada & Entrada_2;  // AND_Gate and_1, 8 bits wide
  assign or_1_out = Entrada | Entrada_2;  // OR_Gate or_1, 8 bits wide
  Multiplexer #(.select(2), .width(8)) multiplexer_1 (
    .in0(adder_1_out), .in1(not_1_out), .in2(and_1_out), .in3(or_1_out), .out(\Saída ),
    .sel(_00___soma__01___NOT__10___OR__11___AND));  // open: en
endmodule
