// Logisim project Calculadora Automática.circ as structural Verilog: 5 circuits, main circuit main
module main (
  input  [15:0] Input,
  output [15:0] Output
);

  wire Clock_out, Reset_out;
  wire [15:0] ACC_q, controlled_buffer_1_out, DR_q, In_q, MAR_q, uc_1_literal, \ula_1_saída ;
  wire [22:0] uc_1_sinais;

  Register #(.width(16)) MAR (
    .D(controlled_buffer_1_out), .Q(MAR_q), .clk(uc_1_sinais[10]), .clr(Reset_out));  // open: en
  Clock Clock (.out(Clock_out));
  Button Reset (.out(Reset_out));
  assign controlled_buffer_1_out = uc_1_sinais[13] ? uc_1_literal : 16'bz;  // Controlled_Buffer controlled_buffer_1
  UC uc_1 (.Clock(Clock_out), .UC_Clear(Reset_out), .Sinais(uc_1_sinais), .Literal(uc_1_literal));
  Register #(.width(16)) In (.D(Input), .Q(In_q), .clk(uc_1_sinais[11]));  // open: en, clr
  RAM #(.addrWidth(16), .dataWidth(16)) ram_1 (
    .addr(MAR_q), .data(controlled_buffer_1_out), .clk(uc_1_sinais[8]), .ld(uc_1_sinais[9]), .clr(Reset_out));  // open: sel
  assign controlled_buffer_1_out = uc_1_sinais[12] ? In_q : 16'bz;  // Controlled_Buffer controlled_buffer_2
  Register #(.width(16)) Out (.D(controlled_buffer_1_out), .Q(Output), .clk(uc_1_sinais[4]));  // open: en, clr
  assign controlled_buffer_1_out = uc_1_sinais[7] ? DR_q : 16'bz;  // Controlled_Buffer controlled_buffer_3
  Register #(.width(16)) DR (.D(controlled_buffer_1_out), .Q(DR_q), .clk(uc_1_sinais[14]));  // open: en, clr
  assign controlled_buffer_1_out = uc_1_sinais[2] ? ACC_q : 16'bz;  // Controlled_Buffer controlled_buffer_4
  ULA ula_1 (
    .ULA_In1(controlled_buffer_1_out), .ULA_In2(ACC_q),
    ._00___Soma___01___NOT___10___AND___11___OR(uc_1_sinais[6:5]), .\Saída (\ula_1_saída ));
  Register #(.width(16)) ACC (.D(\ula_1_saída ), .Q(ACC_q), .clk(uc_1_sinais[1]), .clr(uc_1_sinais[0]));  // open: en

  // Notes on the sheet:
  //   Main Memory (RAM)
endmodule

module ULA (
  input  [15:0] ULA_In1,
  input  [15:0] ULA_In2,
  input  [1:0] _00___Soma___01___NOT___10___AND___11___OR,
  output [15:0] \Saída 
);

  wire [15:0] adder_1_out, and_1_out, not_1_out, or_1_out;

  Adder #(.width(16)) adder_1 (.a(ULA_In1), .b(ULA_In2), .out(adder_1_out));  // open: cin, cout
  assign not_1_out = ~ULA_In1;  // NOT_Gate not_1, 16 bits wide
  assign and_1_out = ULA_In1 & ULA_In2;  // AND_Gate and_1, 16 bits wide
  assign or_1_out = ULA_In1 | ULA_In2;  // OR_Gate or_1, 16 bits wide
  Multiplexer #(.select(2), .width(16)) multiplexer_1 (
    .in0(adder_1_out), .in1(not_1_out), .in2(and_1_out), .in3(or_1_out), .out(\Saída ),
    .sel(_00___Soma___01___NOT___10___AND___11___OR));  // open: en
endmodule

module UC (
  input  Clock,
  input  UC_Clear,
  output [22:0] Sinais,
  output [15:0] Literal
);

  wire and_1_out, and_2_out, divisor_1_t0, divisor_1_t1, not_1_out, or_1_out;
  wire [15:0] \pc_1_endereço__pc ;
  wire [23:0] ram_1_data;

  Divisor divisor_1 (.t0(divisor_1_t0), .t1(divisor_1_t1), .Div_Clear(UC_Clear), .Div_Clock(Clock));  // open: t2, t3
  PC pc_1 (.PC_Clk(divisor_1_t0), .PC_Clear(UC_Clear), .\Endereço__PC (\pc_1_endereço__pc ));
  RAM #(.addrWidth(16), .dataWidth(24)) ram_1 (
    .addr(\pc_1_endereço__pc ), .data(ram_1_data));  // open: sel, clk, ld, clr
  LED u_Literal (.in(ram_1_data[23]));
  Register #(.width(23)) u_Sinais (.D(ram_1_data[22:0]), .Q(Sinais), .clk(and_1_out), .clr(or_1_out));  // open: en
  and and_1 (and_1_out, not_1_out, divisor_1_t1);
  or or_1 (or_1_out, UC_Clear, ram_1_data[23]);
  not not_1 (not_1_out, ram_1_data[23]);
  Register #(.width(16)) Literal_2 (.D(ram_1_data[15:0]), .Q(Literal), .clk(and_2_out), .clr(UC_Clear));  // open: en
  and and_2 (and_2_out, ram_1_data[23], divisor_1_t1);
  LED ACC_Clear (.in(Sinais[0]));
  LED ACC_Clk (.in(Sinais[1]));
  LED ACC_Bus (.in(Sinais[2]));
  LED Compare_Clk (.in(Sinais[3]));
  LED Out_Clk (.in(Sinais[4]));
  LED Open0__ULA (.in(Sinais[5]));
  LED Open1__ULA (.in(Sinais[6]));
  LED DR_Bus (.in(Sinais[7]));
  LED RAM_Clk (.in(Sinais[8]));
  LED RAM_Bus (.in(Sinais[9]));
  LED MAR_Clk (.in(Sinais[10]));
  LED In_Clk (.in(Sinais[11]));
  LED In_Bus (.in(Sinais[12]));
  LED Literal_Bus (.in(Sinais[13]));
  LED DR_clk (.in(Sinais[14]));
endmodule

module PC (
  input  PC_Clk,
  input  PC_Clear,
  output [15:0] \Endereço__PC 
);

  wire [15:0] adder_1_out;

  Adder #(.width(16)) adder_1 (.a(\Endereço__PC ), .b(16'h1), .out(adder_1_out));  // open: cin, cout
  Register #(.width(16)) register_1 (.D(adder_1_out), .Q(\Endereço__PC ), .clk(PC_Clk), .clr(PC_Clear));  // open: en
endmodule

// T
module Divisor (
  input  Div_Clock,
  input  Div_Clear,
  output t0,
  output t1,
  output t2,
  output t3
);

  D_Flip_Flop d_ff_1 (.clk(Div_Clock), .D(t3), .Q(t0), .preset(Div_Clear));  // open: Qn, en, reset
  D_Flip_Flop d_ff_2 (.clk(Div_Clock), .D(t0), .Q(t1), .reset(Div_Clear));  // open: Qn, preset, en
  D_Flip_Flop d_ff_3 (.clk(Div_Clock), .D(t1), .Q(t2), .reset(Div_Clear));  // open: Qn, preset, en
  D_Flip_Flop d_ff_4 (.clk(Div_Clock), .D(t2), .Q(t3), .reset(Div_Clear));  // open: Qn, preset, en
endmodule
