// Logisim project Calculadora Manual.circ as structural Verilog: 4 circuits, main circuit main
module main (
  input  [15:0] Input,
  input  Out_Clk,
  input  DR_Bus,
  input  In_Clk,
  input  In_Bus,
  input  DR_Clk,
  input  [1:0] \Operações ,
  input  MAR_Clk,
  input  RAM_Clk,
  input  RAM_Bus,
  input  ACC_Bus,
  input  ACC_Clk,
  input  AC_Clear,
  output [15:0] Output
);

  wire [15:0] ACC_q, controlled_buffer_1_out, DR_q, In_q, MAR_q, \ula_1_saída ;

  Register #(.width(16)) MAR (.D(controlled_buffer_1_out), .Q(MAR_q), .clk(MAR_Clk));  // open: en, clr
  Register #(.width(16)) In (.D(Input), .Q(In_q), .clk(In_Clk));  // open: en, clr
  assign controlled_buffer_1_out = In_Bus ? In_q : 16'bz;  // Controlled_Buffer controlled_buffer_1
  RAM #(.addrWidth(16), .dataWidth(16)) ram_1 (
    .addr(MAR_q), .data(controlled_buffer_1_out), .clk(RAM_Clk), .ld(RAM_Bus));  // open: sel, clr
  assign controlled_buffer_1_out = DR_Bus ? DR_q : 16'bz;  // Controlled_Buffer controlled_buffer_2
  Register #(.width(16)) DR (.D(controlled_buffer_1_out), .Q(DR_q), .clk(DR_Clk));  // open: en, clr
  assign controlled_buffer_1_out = ACC_Bus ? ACC_q : 16'bz;  // Controlled_Buffer controlled_buffer_3
  Register #(.width(16)) Out (.D(controlled_buffer_1_out), .Q(Output), .clk(Out_Clk));  // open: en, clr
  ULA ula_1 (
    .Entrada_1(controlled_buffer_1_out), .Entrada_2(ACC_q),
    ._00___Soma___01___NOT___10___AND___11___OR(\Operações ), .\Saída (\ula_1_saída ));
  Register #(.width(16)) ACC (.D(\ula_1_saída ), .Q(ACC_q), .clk(ACC_Clk), .clr(AC_Clear));  // open: en

  // Notes on the sheet:
  //   Main Memory
endmodule

module ULA (
  input  [15:0] Entrada_1,
  input  [15:0] Entrada_2,
  input  [1:0] _00___Soma___01___NOT___10___AND___11___OR,
  output [15:0] \Saída 
);

  wire [15:0] adder_1_out, and_1_out, not_1_out, or_1_out;

  Adder #(.width(16)) adder_1 (.a(Entrada_1), .b(Entrada_2), .out(adder_1_out));  // open: cin, cout
  assign not_1_out = ~Entrada_1;  // NOT_Gate not_1, 16 bits wide
  assign and_1_out = Entrada_1 & Entrada_2;  // AND_Gate and_1, 16 bits wide
  assign or_1_out = Entrada_1 | Entrada_2;  // OR_Gate or_1, 16 bits wide
  Multiplexer #(.select(2), .width(16)) multiplexer_1 (
    .in0(adder_1_out), .in1(not_1_out), .in2(and_1_out), .in3(or_1_out), .out(\Saída ),
    .sel(_00___Soma___01___NOT___10___AND___11___OR));  // open: en
endmodule

module UC (
);

  wire Clock_out, Reset_out;
  wire [15:0] \pc_1_endereço ;
  wire [23:0] ram_1_data;

  Clock Clock (.out(Clock_out));
  Button Reset (.out(Reset_out));
  PC pc_1 (.Clock(Clock_out), .reset(Reset_out), .\Endereço (\pc_1_endereço ));
  RAM #(.addrWidth(16), .dataWidth(24)) ram_1 (.addr(\pc_1_endereço ), .data(ram_1_data));  // open: sel, clk, ld, clr
  LED ACC_Clear (.in(ram_1_data[0]));
  LED ACC_Clk (.in(ram_1_data[1]));
  LED ACC_Bus (.in(ram_1_data[2]));
  LED Compare_Clk (.in(ram_1_data[3]));
  LED Out_Clk (.in(ram_1_data[4]));
  LED Open0 (.in(ram_1_data[5]));
  LED Open1 (.in(ram_1_data[6]));
  LED DR_Bus (.in(ram_1_data[7]));
  LED RAM_Clk (.in(ram_1_data[8]));
  LED RAM_Bus (.in(ram_1_data[9]));
  LED MAR_Clk (.in(ram_1_data[10]));
  LED In_Clk (.in(ram_1_data[11]));
  LED In_Bus (.in(ram_1_data[12]));
  LED DR_Clk (.in(ram_1_data[13]));
endmodule

module PC (
  input  Clock,
  input  reset,
  output [15:0] \Endereço 
);

  wire [15:0] adder_1_out, register_1_q;

  Adder #(.width(16)) adder_1 (.a(register_1_q), .b(16'h1), .out(adder_1_out));  // open: cin, cout
  Register #(.width(16)) register_1 (.D(adder_1_out), .Q(register_1_q), .clk(Clock), .clr(reset));  // open: en
  Bit_Extender #(.in_width(16)) bit_extender_1 (.in(register_1_q), .out(\Endereço ));
endmodule
