// Logisim project Clock Divisor de Frequência.circ as structural Verilog: 1 circuit, main circuit main
module main (
  input  reset,
  output t1,
  output t2,
  output t3,
  output t0
);

  wire clock_out;

  Clock clock (.out(clock_out));
  D_Flip_Flop d_ff_1 (.clk(clock_out), .D(t3), .Q(t0), .preset(reset));  // open: Qn, en, reset
  D_Flip_Flop d_ff_2 (.clk(clock_out), .D(t0), .Q(t1), .reset(reset));  // open: Qn, preset, en
  D_Flip_Flop d_ff_3 (.clk(clock_out), .D(t1), .Q(t2), .reset(reset));  // open: Qn, preset, en
  D_Flip_Flop d_ff_4 (.clk(clock_out), .D(t2), .Q(t3), .reset(reset));  // open: Qn, preset, en
endmodule
