// Logisim project Contador de Programa.circ as structural Verilog: 1 circuit, main circuit main
module main (
  input  reset,
  output [15:0] \Endereço 
);

  wire clock_out;
  wire [15:0] adder_1_out;

  Clock clock (.out(clock_out));
  Adder #(.width(16)) adder_1 (.a(\Endereço ), .b(16'h1), .out(adder_1_out));  // open: cin, cout
  Register #(.width(16)) register_1 (.D(adder_1_out), .Q(\Endereço ), .clk(clock_out), .clr(reset));  // open: en
endmodule
